// Logisim project main.circ as structural Verilog: 9 circuits, main circuit main
module main (
  input  in_1,
  output out_2
);

  // not not_1: pin names not known; wires that end beside it: in_1, out_2
endmodule

module \and  (
  input  X,
  input  Y,
  output out_3
);

  wire transistor_1_out;

  Transistor #(.\type ("n")) transistor_1 (.in(1'b1), .out(transistor_1_out), .gate(X));
  Transistor #(.\type ("n")) transistor_2 (.in(transistor_1_out), .out(out_3), .gate(Y));
  Transistor transistor_3 (.in(1'b0), .out(out_3), .gate(X));
  Transistor transistor_4 (.in(1'b0), .out(out_3), .gate(Y));
endmodule

module \or  (
  input  X,
  input  Y,
  output out_3
);

  wire transistor_3_out;

  Transistor #(.\type ("n")) transistor_1 (.in(1'b1), .out(out_3), .gate(X));
  Transistor transistor_2 (.in(transistor_3_out), .out(out_3), .gate(X));
  Transistor transistor_3 (.in(1'b0), .out(transistor_3_out), .gate(Y));
  Transistor #(.\type ("n")) transistor_4 (.in(1'b1), .out(out_3), .gate(Y));
endmodule

module \not  (
  input  X,
  output out_2
);

  Transistor transistor_1 (.in(1'b1), .out(out_2), .gate(X));
  Transistor #(.\type ("n")) transistor_2 (.in(1'b0), .out(out_2), .gate(X));
endmodule

module Xand (
  input  X,
  input  Y,
  output out_3
);

  wire transistor_3_out;

  Transistor transistor_1 (.in(1'b1), .out(out_3), .gate(X));
  Transistor #(.\type ("n")) transistor_2 (.in(transistor_3_out), .out(out_3), .gate(X));
  Transistor #(.\type ("n")) transistor_3 (.in(1'b0), .out(transistor_3_out), .gate(Y));
  Transistor transistor_4 (.in(1'b1), .out(out_3), .gate(Y));
endmodule

module Xor (
  input  X,
  input  Y,
  output out_3
);

  wire transistor_1_out;

  Transistor transistor_1 (.in(1'b1), .out(transistor_1_out), .gate(X));
  Transistor transistor_2 (.in(transistor_1_out), .out(out_3), .gate(Y));
  Transistor #(.\type ("n")) transistor_3 (.in(1'b0), .out(out_3), .gate(X));
  Transistor #(.\type ("n")) transistor_4 (.in(1'b0), .out(out_3), .gate(Y));
endmodule

module No_A_o_B (
  input  A,
  input  B,
  output out_3
);

  wire not_1_out_2;

  \not  not_1 (.X(A), .out_2(not_1_out_2));
  \or  or_1 (.X(not_1_out_2), .Y(B), .out_3(out_3));
endmodule

module A_Y_NO_B__O__NO_A_Y_B (
  input  A,
  input  B,
  output out_3
);

  wire and_1_out_3, and_2_out_3, not_1_out_2, not_2_out_2;

  \not  not_1 (.X(A), .out_2(not_1_out_2));
  \not  not_2 (.X(B), .out_2(not_2_out_2));
  \and  and_1 (.X(B), .Y(not_1_out_2), .out_3(and_1_out_3));
  \and  and_2 (.X(not_2_out_2), .Y(A), .out_3(and_2_out_3));
  \or  or_1 (.X(and_1_out_3), .Y(and_2_out_3), .out_3(out_3));
endmodule

module Primo (
);

  DotMatrix dotmatrix_1 ();  // open: col0, col1, col2, col3, col4
  Button _0 ();  // open: out
  TTY tty_1 ();  // open: data, clk, we, clr
endmodule
